# Fritzing sketch baro_humidity (saved by Fritzing 0.9.3b)
breadboards: 1

parts:
  WeMos_D1_Mini1 = WeMos D1 Mini
  RHT1 = Humidity and Temperature Sensor RHT03
  Part2 = Adafruit BMP180
  R1 = Resistor [tolerance=±5% resistance=10k package="0603 [SMD]"]

nets:
  N1: WeMos_D1_Mini1.D2, Part2.SDA
  N2: RHT1.Vcc, R1.Pin_1
  N3: RHT1.Data-signal, R1.Pin_0

custom parts:
  Adafruit BMP180: This precision sensor from Bosch is the best low-cost sensing solution for measuring barometric pressure and temperature. Because pressure changes with altitude you can also use it as an altimeter! The sensor is soldered onto a PCB with a 3.3V regulator, I2C level shifter and pull-up resistors on the I2C pins. The BMP180 is the next-generation of sensors from Bosch, and replaces the BMP085.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
